# Fritzing sketch 2024-06-21 Altimeter (saved by Fritzing 1.0.2b)
perfboards: 1

parts:
  U1 = LuaNode32 / ESP32 [part_number=ESP32S-PIN30]
  Home_switch = Round Pushbutton
  LCD1 = Waveshare 1.28 inch Round 240x240 LCD Display
  SG1 = Buzzer 12mm [part_number=COM-07950 package=buzzer-12mm-ns]
  Composant1 = Barometric Pressure Sensor - BMP180 Breakout (GY-68)
  S2 = Pushbutton [package="[THT]"]
  BAT1 = Battery Holders [package=lipo-1100mAh]
  R1 = Trimmer Potentiometer [maximum_resistance=10kΩ knob_status=50% power=0.5W package=THT]
  S3 = Taiway 100-SP-X-T1 SPDT Miniature Toggle Switch [part_number=100-SP-X-T1-0-0-B1-M2 package=THT]
  LED1 = LED - 5mm [color="Blue (525nm)" current=0.030A package="5 mm [THT]"]
  R2 = Resistor [tolerance=±5% power=0.25W resistance=1000 package=THT]

nets:
  GND: U1.GND, LCD1.pin2, Composant1.GND, R1.leg2, S3.L1, LED1.cathode
  N1: U1.D15, Home_switch.leg0
  N2: U1.TX2, SG1.1
  N3: U1.D21, Composant1.SDA
  N4: U1.D22, Composant1.SCL
  N5: SG1.2, R1.wiper
  N6: Composant1.VCC, BAT1.+, R2.Pin_0
  N7: S2.Pin_1, S2.Pin_2
  N8: S2.Pin_3, S2.Pin_4
  N9: BAT1.-, S3.L2
  N10: LED1.anode, R2.Pin_1

custom parts:
  LuaNode32 / ESP32: New Image for LuaNode32 DOIT ESP32 DEVKIT V1. Base parts from LuaNode32 / ESP32 ESP32 based LuaNode32 by G.Noorlander DOIT Esp32 DevKit v1 (30 pins long, 11 pins width) by Werner Rothschopf (modified by vanepp Dec 2018)
  Waveshare 1.28 inch Round 240x240 LCD Display: Waveshare 1.28 inch Round 240x240 LCD Display with GC9A01 Controller
  Buzzer 12mm: Buzzer 12mm Spark Fun Electronics SKU : Comp-Buzzer Through hole This is a small 12mm round speaker that operates around the audible 2kHz range. You can use these speakers to create simple music or user interfaces. This is not a true piezoelectric speaker but behaves similarly. Instead of a piezoelectric crystal that vibrates with an electric current, this tiny speaker uses an electromagnet to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
