# Fritzing sketch 2024-10-24 Altimeter v0.03 (saved by Fritzing 1.0.2b)
circuit board: 4.41881cm x 7.41637cm
perfboards: 1

parts:
  ESP_WROOM32_DEVELOPMENT_KIT = LuaNode32 / ESP32 [part_number=ESP32S-PIN30]
  Buzzer = Buzzer 12mm [part_number=COM-07950 package=buzzer-12mm-ns]
  BPM180 = Barometric Pressure Sensor - BMP180 Breakout (GY-68)
  BAT1 = Battery Holders [package=lipo-1100mAh]
  R1 = Trimmer Potentiometer [maximum_resistance=10kΩ knob_status=50% power=0.5W package=THT]
  S3 = Taiway 100-SP-X-T1 SPDT Miniature Toggle Switch [part_number=100-SP-X-T1-0-0-B1-M2 package=THT]
  - = Pushbutton [package="[THT]"]
  + = Pushbutton [package="[THT]"]
  Batt = female pin header, 2 pins [form="♀ (female)"]
  GC9A01_TFT_240x240_SPI = female pin header, 7 pins [form="♀ (female)"]

nets:
  GND: ESP_WROOM32_DEVELOPMENT_KIT.GND, BPM180.GND, R1.leg2, S3.L1, -.Pin_3, -.Pin_4, +.Pin_3, +.Pin_4, Batt.pin2, GC9A01_TFT_240x240_SPI.pin2
  VIN: ESP_WROOM32_DEVELOPMENT_KIT.Vin, BPM180.VCC, BAT1.+, Batt.pin1
  N1: ESP_WROOM32_DEVELOPMENT_KIT.3V3, GC9A01_TFT_240x240_SPI.pin1
  N2: ESP_WROOM32_DEVELOPMENT_KIT.D15, -.Pin_1, -.Pin_2
  N3: ESP_WROOM32_DEVELOPMENT_KIT.D2, GC9A01_TFT_240x240_SPI.pin5
  N4: ESP_WROOM32_DEVELOPMENT_KIT.D4, GC9A01_TFT_240x240_SPI.pin6
  N5: ESP_WROOM32_DEVELOPMENT_KIT.RX2, +.Pin_1, +.Pin_2
  N6: ESP_WROOM32_DEVELOPMENT_KIT.TX2, Buzzer.1
  N7: ESP_WROOM32_DEVELOPMENT_KIT.D18, GC9A01_TFT_240x240_SPI.pin3
  N8: ESP_WROOM32_DEVELOPMENT_KIT.D21, BPM180.SDA
  N9: ESP_WROOM32_DEVELOPMENT_KIT.D22, BPM180.SCL
  N10: ESP_WROOM32_DEVELOPMENT_KIT.D23, GC9A01_TFT_240x240_SPI.pin4
  N11: Buzzer.2, R1.wiper
  N12: BAT1.-, S3.COM

notes:
  3.3V
  GND
  SCL / CLK
  SDA / MOSI
  DC
  CS
  SCL
  SDA
  3V-5V VCC
  5V
  x
  Altimeter
  by Hippo
  v1.00

custom parts:
  LuaNode32 / ESP32: New Image for LuaNode32 DOIT ESP32 DEVKIT V1. Base parts from LuaNode32 / ESP32 ESP32 based LuaNode32 by G.Noorlander DOIT Esp32 DevKit v1 (30 pins long, 11 pins width) by Werner Rothschopf (modified by vanepp Dec 2018)
  Buzzer 12mm: Buzzer 12mm Spark Fun Electronics SKU : Comp-Buzzer Through hole This is a small 12mm round speaker that operates around the audible 2kHz range. You can use these speakers to create simple music or user interfaces. This is not a true piezoelectric speaker but behaves similarly. Instead of a piezoelectric crystal that vibrates with an electric current, this tiny speaker uses an electromagnet to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
